// Logisim project Project.circ as structural Verilog
module Register_File_cba136b5 (
  input  [4:0] Read_Register_2_7d3cba4f,
  input  [4:0] Read_Register_1_4aa6ffe9,
  input  [31:0] Write_data_f7cafedb,
  input  [4:0] Write_Register,
  input  RegWrite,
  output [31:0] Read_Data1_73ecfc59,
  output [31:0] Read_Data_2_0166a1d0
);

  wire and_1_out, and_2_out, and_3_out, and_4_out, and_5_out, and_6_out, and_7_out, and_8_out, and_9_out,
       and_10_out, and_11_out, and_12_out, and_13_out, and_14_out, and_15_out, and_16_out, and_17_out,
       and_18_out, and_19_out, and_20_out, and_21_out, and_22_out, and_23_out, and_24_out, and_25_out,
       and_26_out, and_27_out, and_28_out, and_29_out, and_30_out, and_31_out, and_32_out, clock_1_out,
       decoder_1_out0, decoder_1_out1, decoder_1_out2, decoder_1_out3, decoder_1_out4, decoder_1_out5,
       decoder_1_out6, decoder_1_out7, decoder_1_out8, decoder_1_out9, decoder_1_out10, decoder_1_out11,
       decoder_1_out12, decoder_1_out13, decoder_1_out14, decoder_1_out15, decoder_1_out16, decoder_1_out17,
       decoder_1_out18, decoder_1_out19, decoder_1_out20, decoder_1_out21, decoder_1_out22, decoder_1_out23,
       decoder_1_out24, decoder_1_out25, decoder_1_out26, decoder_1_out27, decoder_1_out28, decoder_1_out29,
       decoder_1_out30, decoder_1_out31;
  wire [31:0] register_1_p4, register_2_p7, register_3_p7, register_4_p7, register_4_p8, register_5_p8,
       register_6_p8, register_6_p9, register_7_p9, register_10_p7, register_11_p7, register_12_p7,
       register_13_p7, register_14_p7, register_15_p7, register_16_p7, register_17_p7, register_18_p7,
       register_19_p7, register_20_p7, register_21_p7, register_22_p7, register_23_p7, register_24_p7,
       register_25_p7, register_26_p7, register_27_p7, register_28_p7, register_29_p7, register_30_p7,
       register_31_p7, register_32_p7;

  Decoder #(.select(5), .enable("false")) decoder_1 (
    .out0(decoder_1_out0), .out1(decoder_1_out1), .out2(decoder_1_out2), .out3(decoder_1_out3),
    .out4(decoder_1_out4), .out5(decoder_1_out5), .out6(decoder_1_out6), .out7(decoder_1_out7),
    .out8(decoder_1_out8), .out9(decoder_1_out9), .out10(decoder_1_out10), .out11(decoder_1_out11),
    .out12(decoder_1_out12), .out13(decoder_1_out13), .out14(decoder_1_out14), .out15(decoder_1_out15),
    .out16(decoder_1_out16), .out17(decoder_1_out17), .out18(decoder_1_out18), .out19(decoder_1_out19),
    .out20(decoder_1_out20), .out21(decoder_1_out21), .out22(decoder_1_out22), .out23(decoder_1_out23),
    .out24(decoder_1_out24), .out25(decoder_1_out25), .out26(decoder_1_out26), .out27(decoder_1_out27),
    .out28(decoder_1_out28), .out29(decoder_1_out29), .out30(decoder_1_out30), .out31(decoder_1_out31),
    .sel(Write_Register));
  and and_1 (and_1_out, decoder_1_out0, RegWrite);
  and and_2 (and_2_out, decoder_1_out1, RegWrite);
  and and_3 (and_3_out, decoder_1_out2, RegWrite);
  and and_4 (and_4_out, decoder_1_out3, RegWrite);
  and and_5 (and_5_out, decoder_1_out4, RegWrite);
  and and_6 (and_6_out, decoder_1_out5, RegWrite);
  and and_7 (and_7_out, decoder_1_out6, RegWrite);
  and and_8 (and_8_out, decoder_1_out7, RegWrite);
  and and_9 (and_9_out, decoder_1_out8, RegWrite);
  and and_10 (and_10_out, decoder_1_out9, RegWrite);
  and and_11 (and_11_out, decoder_1_out10, RegWrite);
  and and_12 (and_12_out, decoder_1_out11, RegWrite);
  and and_13 (and_13_out, decoder_1_out12, RegWrite);
  and and_14 (and_14_out, decoder_1_out13, RegWrite);
  and and_15 (and_15_out, decoder_1_out14, RegWrite);
  and and_16 (and_16_out, decoder_1_out15, RegWrite);
  and and_17 (and_17_out, decoder_1_out16, RegWrite);
  and and_18 (and_18_out, decoder_1_out17, RegWrite);
  and and_19 (and_19_out, decoder_1_out18, RegWrite);
  and and_20 (and_20_out, decoder_1_out19, RegWrite);
  and and_21 (and_21_out, decoder_1_out20, RegWrite);
  and and_22 (and_22_out, decoder_1_out21, RegWrite);
  and and_23 (and_23_out, decoder_1_out22, RegWrite);
  and and_24 (and_24_out, decoder_1_out23, RegWrite);
  and and_25 (and_25_out, decoder_1_out24, RegWrite);
  and and_26 (and_26_out, decoder_1_out25, RegWrite);
  and and_27 (and_27_out, decoder_1_out26, RegWrite);
  and and_28 (and_28_out, decoder_1_out27, RegWrite);
  and and_29 (and_29_out, decoder_1_out28, RegWrite);
  and and_30 (and_30_out, decoder_1_out29, RegWrite);
  and and_31 (and_31_out, decoder_1_out30, RegWrite);
  and and_32 (and_32_out, decoder_1_out31, RegWrite);
  Clock clock_1 (.out(clock_1_out));
  // Register #(.width(32)) register_1: pin names not known; wires that end beside it: {32{1'b0}}, and_1_out, clock_1_out, register_1_p4
  // Register #(.width(32)) register_2: pin names not known; wires that end beside it: {32{1'b0}}, and_1_out, Write_data_f7cafedb, and_2_out, clock_1_out, clock_1_out, register_2_p7
  // Register #(.width(32)) register_3: pin names not known; wires that end beside it: Write_data_f7cafedb, and_2_out, Write_data_f7cafedb, and_3_out, clock_1_out, clock_1_out, register_3_p7
  // Register #(.width(32)) register_4: pin names not known; wires that end beside it: Write_data_f7cafedb, and_3_out, Write_data_f7cafedb, and_4_out, clock_1_out, clock_1_out, register_4_p7, register_4_p8
  // Register #(.width(32)) register_5: pin names not known; wires that end beside it: Write_data_f7cafedb, and_5_out, Write_data_f7cafedb, and_6_out, clock_1_out, clock_1_out, clock_1_out, register_5_p8, register_4_p8
  // Register #(.width(32)) register_6: pin names not known; wires that end beside it: Write_data_f7cafedb, and_6_out, Write_data_f7cafedb, and_7_out, clock_1_out, clock_1_out, clock_1_out, register_6_p8, register_6_p9
  // Register #(.width(32)) register_7: pin names not known; wires that end beside it: Write_data_f7cafedb, and_7_out, Write_data_f7cafedb, and_8_out, clock_1_out, clock_1_out, clock_1_out, register_6_p9, register_7_p9
  // Register #(.width(32), .trigger("high")) register_8: pin names not known; wires that end beside it: Write_data_f7cafedb, and_8_out, Write_data_f7cafedb, and_9_out, clock_1_out, clock_1_out, clock_1_out, register_7_p9, register_7_p9
  // Register #(.width(32)) register_9: pin names not known; wires that end beside it: Write_data_f7cafedb, and_8_out, Write_data_f7cafedb, and_9_out, clock_1_out, clock_1_out, register_7_p9
  // Register #(.width(32)) register_10: pin names not known; wires that end beside it: Write_data_f7cafedb, and_9_out, Write_data_f7cafedb, and_10_out, clock_1_out, clock_1_out, register_10_p7
  // Register #(.width(32)) register_11: pin names not known; wires that end beside it: Write_data_f7cafedb, and_10_out, Write_data_f7cafedb, and_11_out, clock_1_out, clock_1_out, register_11_p7
  // Register #(.width(32)) register_12: pin names not known; wires that end beside it: Write_data_f7cafedb, and_11_out, Write_data_f7cafedb, and_12_out, clock_1_out, clock_1_out, register_12_p7
  // Register #(.width(32)) register_13: pin names not known; wires that end beside it: Write_data_f7cafedb, and_12_out, Write_data_f7cafedb, and_13_out, clock_1_out, clock_1_out, register_13_p7
  // Register #(.width(32)) register_14: pin names not known; wires that end beside it: Write_data_f7cafedb, and_13_out, Write_data_f7cafedb, and_14_out, clock_1_out, clock_1_out, register_14_p7
  // Register #(.width(32)) register_15: pin names not known; wires that end beside it: Write_data_f7cafedb, and_14_out, Write_data_f7cafedb, and_15_out, clock_1_out, clock_1_out, register_15_p7
  // Register #(.width(32)) register_16: pin names not known; wires that end beside it: Write_data_f7cafedb, and_15_out, Write_data_f7cafedb, and_16_out, clock_1_out, clock_1_out, register_16_p7
  // Register #(.width(32)) register_17: pin names not known; wires that end beside it: Write_data_f7cafedb, and_16_out, Write_data_f7cafedb, and_17_out, clock_1_out, clock_1_out, register_17_p7
  // Register #(.width(32)) register_18: pin names not known; wires that end beside it: Write_data_f7cafedb, and_17_out, Write_data_f7cafedb, and_18_out, clock_1_out, clock_1_out, register_18_p7
  // Register #(.width(32)) register_19: pin names not known; wires that end beside it: Write_data_f7cafedb, and_18_out, Write_data_f7cafedb, and_19_out, clock_1_out, clock_1_out, register_19_p7
  // Register #(.width(32)) register_20: pin names not known; wires that end beside it: Write_data_f7cafedb, and_19_out, Write_data_f7cafedb, and_20_out, clock_1_out, clock_1_out, register_20_p7
  // Register #(.width(32)) register_21: pin names not known; wires that end beside it: Write_data_f7cafedb, and_20_out, Write_data_f7cafedb, and_21_out, clock_1_out, clock_1_out, register_21_p7
  // Register #(.width(32)) register_22: pin names not known; wires that end beside it: Write_data_f7cafedb, and_21_out, clock_1_out, Write_data_f7cafedb, and_22_out, clock_1_out, register_22_p7
  // Register #(.width(32)) register_23: pin names not known; wires that end beside it: Write_data_f7cafedb, and_22_out, Write_data_f7cafedb, and_23_out, clock_1_out, clock_1_out, register_23_p7
  // Register #(.width(32)) register_24: pin names not known; wires that end beside it: Write_data_f7cafedb, and_23_out, Write_data_f7cafedb, and_24_out, clock_1_out, clock_1_out, register_24_p7
  // Register #(.width(32)) register_25: pin names not known; wires that end beside it: Write_data_f7cafedb, and_24_out, Write_data_f7cafedb, and_25_out, clock_1_out, clock_1_out, register_25_p7
  // Register #(.width(32)) register_26: pin names not known; wires that end beside it: Write_data_f7cafedb, and_25_out, Write_data_f7cafedb, and_26_out, clock_1_out, clock_1_out, register_26_p7
  // Register #(.width(32)) register_27: pin names not known; wires that end beside it: Write_data_f7cafedb, and_26_out, Write_data_f7cafedb, and_27_out, clock_1_out, clock_1_out, register_27_p7
  // Register #(.width(32)) register_28: pin names not known; wires that end beside it: Write_data_f7cafedb, and_27_out, Write_data_f7cafedb, and_28_out, clock_1_out, clock_1_out, register_28_p7
  // Register #(.width(32)) register_29: pin names not known; wires that end beside it: Write_data_f7cafedb, and_28_out, Write_data_f7cafedb, and_29_out, clock_1_out, clock_1_out, register_29_p7
  // Register #(.width(32)) register_30: pin names not known; wires that end beside it: Write_data_f7cafedb, and_29_out, Write_data_f7cafedb, and_30_out, clock_1_out, clock_1_out, register_30_p7
  // Register #(.width(32)) register_31: pin names not known; wires that end beside it: Write_data_f7cafedb, and_30_out, Write_data_f7cafedb, and_31_out, clock_1_out, clock_1_out, register_31_p7
  // Register #(.width(32)) register_32: pin names not known; wires that end beside it: Write_data_f7cafedb, and_31_out, Write_data_f7cafedb, and_32_out, clock_1_out, clock_1_out, register_32_p7
  Multiplexer #(.select(5), .width(32), .enable("false")) multiplexer_1 (
    .in0(register_1_p4), .in1(register_2_p7), .in2(register_3_p7), .in3(register_4_p7), .in4(register_4_p8),
    .in5(register_5_p8), .in6(register_6_p8), .in7(register_6_p9), .in8(register_7_p9), .in9(register_10_p7),
    .in10(register_11_p7), .in11(register_12_p7), .in12(register_13_p7), .in13(register_14_p7),
    .in14(register_15_p7), .in15(register_16_p7), .in16(register_17_p7), .in17(register_18_p7),
    .in18(register_19_p7), .in19(register_20_p7), .in20(register_21_p7), .in21(register_22_p7),
    .in22(register_23_p7), .in23(register_24_p7), .in24(register_25_p7), .in25(register_26_p7),
    .in26(register_27_p7), .in27(register_28_p7), .in28(register_29_p7), .in29(register_30_p7),
    .in30(register_31_p7), .in31(register_32_p7), .out(Read_Data1_73ecfc59), .sel(Read_Register_1_4aa6ffe9));
  Multiplexer #(.select(5), .width(32), .enable("false")) multiplexer_2 (
    .in0(register_1_p4), .in1(register_2_p7), .in2(register_3_p7), .in3(register_4_p7), .in4(register_4_p8),
    .in5(register_5_p8), .in6(register_6_p8), .in7(register_6_p9), .in8(register_7_p9), .in9(register_10_p7),
    .in10(register_11_p7), .in11(register_12_p7), .in12(register_13_p7), .in13(register_14_p7),
    .in14(register_15_p7), .in15(register_16_p7), .in16(register_17_p7), .in17(register_18_p7),
    .in18(register_19_p7), .in19(register_20_p7), .in20(register_21_p7), .in21(register_22_p7),
    .in22(register_23_p7), .in23(register_24_p7), .in24(register_25_p7), .in25(register_26_p7),
    .in26(register_27_p7), .in27(register_28_p7), .in28(register_29_p7), .in29(register_30_p7),
    .in30(register_31_p7), .in31(register_32_p7), .out(Read_Data_2_0166a1d0), .sel(Read_Register_2_7d3cba4f));

  // Notes on the sheet:
  //   Clock
endmodule

module ALU (
  input  [31:0] A,
  input  [31:0] B,
  input  in_3,
  input  [2:0] Operation,
  input  Bslc,
  input  Aslc,
  input  [1:0] opreation,
  output Zeroflag,
  output [31:0] Aluout,
  output overflow,
  output Cout
);

  wire alu_1_bit_unit_099431f7_1_cout, alu_1_bit_unit_099431f7_2_cout, alu_1_bit_unit_099431f7_3_cout,
       alu_1_bit_unit_099431f7_4_cout, alu_1_bit_unit_099431f7_5_cout, alu_1_bit_unit_099431f7_6_cout,
       alu_1_bit_unit_099431f7_7_cout, alu_1_bit_unit_099431f7_8_cout, alu_1_bit_unit_099431f7_9_cout,
       alu_1_bit_unit_099431f7_10_cout, alu_1_bit_unit_099431f7_11_cout, alu_1_bit_unit_099431f7_12_cout,
       alu_1_bit_unit_099431f7_13_cout, alu_1_bit_unit_099431f7_14_cout, alu_1_bit_unit_099431f7_15_cout,
       alu_1_bit_unit_099431f7_16_cout, alu_1_bit_unit_099431f7_17_cout, alu_1_bit_unit_099431f7_18_cout,
       alu_1_bit_unit_099431f7_19_cout, alu_1_bit_unit_099431f7_20_cout, alu_1_bit_unit_099431f7_21_cout,
       alu_1_bit_unit_099431f7_22_cout, alu_1_bit_unit_099431f7_23_cout, alu_1_bit_unit_099431f7_24_cout,
       alu_1_bit_unit_099431f7_25_cout, alu_1_bit_unit_099431f7_26_cout, alu_1_bit_unit_099431f7_27_cout,
       alu_1_bit_unit_099431f7_28_cout, alu_1_bit_unit_099431f7_29_cout, alu_1_bit_unit_099431f7_30_cout,
       alu_1_bit_unit_099431f7_31_cout, comparator_1_eq, comparator_1_gt, comparator_1_lt, comparator_2_eq,
       comparator_2_gt, comparator_2_lt, not_1_out, not_2_out, not_3_out, not_4_out, or_1_out, R0, R1, R2,
       R3, R4, R5, R6, R7, R8, R9, R10, R11, R12, R13, R14, R15, R16, R17, R18, R19, R20, R21, R22, R23, R24,
       R25, R26, R27, R28, R29, R30, R31, sign_out, unsign_out;
  wire [31:0] bit_extender_1_out, bit_extender_2_out, bit_extender_3_out, shifter_1_out, shifter_2_out,
       shifter_3_out, shifter_4_out;

  ALU_1_bit_unit_099431f7 alu_1_bit_unit_099431f7_1 (
    .A(A[0]), .B(B[0]), .cin(in_3), .reselt(R0), .cout(alu_1_bit_unit_099431f7_1_cout), .Aslc(Aslc),
    .Bslc(Bslc), .operation(opreation));
  ALU_1_bit_unit_099431f7 alu_1_bit_unit_099431f7_2 (
    .A(A[1]), .B(B[1]), .cin(alu_1_bit_unit_099431f7_1_cout), .reselt(R1),
    .cout(alu_1_bit_unit_099431f7_2_cout), .Aslc(Aslc), .Bslc(Bslc), .operation(opreation));
  ALU_1_bit_unit_099431f7 alu_1_bit_unit_099431f7_3 (
    .A(A[2]), .B(B[2]), .cin(alu_1_bit_unit_099431f7_2_cout), .reselt(R2),
    .cout(alu_1_bit_unit_099431f7_3_cout), .Aslc(Aslc), .Bslc(Bslc), .operation(opreation));
  ALU_1_bit_unit_099431f7 alu_1_bit_unit_099431f7_4 (
    .A(A[3]), .B(B[3]), .cin(alu_1_bit_unit_099431f7_3_cout), .reselt(R3),
    .cout(alu_1_bit_unit_099431f7_4_cout), .Aslc(Aslc), .Bslc(Bslc), .operation(opreation));
  ALU_1_bit_unit_099431f7 alu_1_bit_unit_099431f7_5 (
    .A(A[4]), .B(B[4]), .cin(alu_1_bit_unit_099431f7_4_cout), .reselt(R4),
    .cout(alu_1_bit_unit_099431f7_5_cout), .Aslc(Aslc), .Bslc(Bslc));  // open: operation
  ALU_1_bit_unit_099431f7 alu_1_bit_unit_099431f7_6 (
    .A(A[5]), .B(B[5]), .cin(alu_1_bit_unit_099431f7_5_cout), .reselt(R5),
    .cout(alu_1_bit_unit_099431f7_6_cout), .Aslc(Aslc), .Bslc(Bslc), .operation(opreation));
  ALU_1_bit_unit_099431f7 alu_1_bit_unit_099431f7_7 (
    .A(A[6]), .B(B[6]), .cin(alu_1_bit_unit_099431f7_6_cout), .reselt(R6),
    .cout(alu_1_bit_unit_099431f7_7_cout), .Aslc(Aslc), .Bslc(Bslc), .operation(opreation));
  ALU_1_bit_unit_099431f7 alu_1_bit_unit_099431f7_8 (
    .A(A[7]), .B(B[7]), .cin(alu_1_bit_unit_099431f7_7_cout), .reselt(R7),
    .cout(alu_1_bit_unit_099431f7_8_cout), .Aslc(Aslc), .Bslc(Bslc), .operation(opreation));
  ALU_1_bit_unit_099431f7 alu_1_bit_unit_099431f7_9 (
    .A(A[8]), .B(B[8]), .cin(alu_1_bit_unit_099431f7_8_cout), .reselt(R8),
    .cout(alu_1_bit_unit_099431f7_9_cout), .Aslc(Aslc), .Bslc(Bslc), .operation(opreation));
  ALU_1_bit_unit_099431f7 alu_1_bit_unit_099431f7_10 (
    .A(A[9]), .B(B[9]), .cin(alu_1_bit_unit_099431f7_9_cout), .reselt(R9),
    .cout(alu_1_bit_unit_099431f7_10_cout), .Aslc(Aslc), .Bslc(Bslc), .operation(opreation));
  ALU_1_bit_unit_099431f7 alu_1_bit_unit_099431f7_11 (
    .A(A[10]), .B(B[10]), .cin(alu_1_bit_unit_099431f7_10_cout), .reselt(R10),
    .cout(alu_1_bit_unit_099431f7_11_cout), .Aslc(Aslc), .Bslc(Bslc), .operation(opreation));
  ALU_1_bit_unit_099431f7 alu_1_bit_unit_099431f7_12 (
    .A(A[11]), .B(B[11]), .cin(alu_1_bit_unit_099431f7_11_cout), .reselt(R11),
    .cout(alu_1_bit_unit_099431f7_12_cout), .Aslc(Aslc), .Bslc(Bslc), .operation(opreation));
  ALU_1_bit_unit_099431f7 alu_1_bit_unit_099431f7_13 (
    .A(A[12]), .B(B[12]), .cin(alu_1_bit_unit_099431f7_12_cout), .reselt(R12),
    .cout(alu_1_bit_unit_099431f7_13_cout), .Bslc(Bslc), .operation(opreation));  // open: Aslc
  ALU_1_bit_unit_099431f7 alu_1_bit_unit_099431f7_14 (
    .A(A[13]), .B(B[13]), .cin(alu_1_bit_unit_099431f7_13_cout), .reselt(R13),
    .cout(alu_1_bit_unit_099431f7_14_cout), .Aslc(Aslc), .Bslc(Bslc), .operation(opreation));
  ALU_1_bit_unit_099431f7 alu_1_bit_unit_099431f7_15 (
    .A(A[14]), .B(B[14]), .cin(alu_1_bit_unit_099431f7_14_cout), .reselt(R14),
    .cout(alu_1_bit_unit_099431f7_15_cout), .Aslc(Aslc), .Bslc(Bslc), .operation(opreation));
  ALU_1_bit_unit_099431f7 alu_1_bit_unit_099431f7_16 (
    .A(A[15]), .B(B[15]), .cin(alu_1_bit_unit_099431f7_15_cout), .reselt(R15),
    .cout(alu_1_bit_unit_099431f7_16_cout), .Aslc(Aslc), .Bslc(Bslc), .operation(opreation));
  ALU_1_bit_unit_099431f7 alu_1_bit_unit_099431f7_17 (
    .A(A[16]), .B(B[16]), .cin(alu_1_bit_unit_099431f7_16_cout), .reselt(R16),
    .cout(alu_1_bit_unit_099431f7_17_cout), .Aslc(Aslc), .Bslc(Bslc), .operation(opreation));
  ALU_1_bit_unit_099431f7 alu_1_bit_unit_099431f7_18 (
    .A(A[17]), .B(B[17]), .cin(alu_1_bit_unit_099431f7_17_cout), .reselt(R17),
    .cout(alu_1_bit_unit_099431f7_18_cout), .Aslc(Aslc), .Bslc(Bslc), .operation(opreation));
  ALU_1_bit_unit_099431f7 alu_1_bit_unit_099431f7_19 (
    .A(A[18]), .B(B[18]), .cin(alu_1_bit_unit_099431f7_18_cout), .reselt(R18),
    .cout(alu_1_bit_unit_099431f7_19_cout), .Aslc(Aslc), .Bslc(Bslc), .operation(opreation));
  ALU_1_bit_unit_099431f7 alu_1_bit_unit_099431f7_20 (
    .A(A[19]), .B(B[19]), .cin(alu_1_bit_unit_099431f7_19_cout), .reselt(R19),
    .cout(alu_1_bit_unit_099431f7_20_cout), .Aslc(Aslc), .Bslc(Bslc), .operation(opreation));
  ALU_1_bit_unit_099431f7 alu_1_bit_unit_099431f7_21 (
    .A(A[20]), .B(B[20]), .cin(alu_1_bit_unit_099431f7_20_cout), .reselt(R20),
    .cout(alu_1_bit_unit_099431f7_21_cout), .Aslc(Aslc), .Bslc(Bslc), .operation(opreation));
  ALU_1_bit_unit_099431f7 alu_1_bit_unit_099431f7_22 (
    .A(A[21]), .B(B[21]), .cin(alu_1_bit_unit_099431f7_21_cout), .reselt(R21),
    .cout(alu_1_bit_unit_099431f7_22_cout), .Aslc(Aslc), .Bslc(Bslc), .operation(opreation));
  ALU_1_bit_unit_099431f7 alu_1_bit_unit_099431f7_23 (
    .A(A[22]), .B(B[22]), .cin(alu_1_bit_unit_099431f7_22_cout), .reselt(R22),
    .cout(alu_1_bit_unit_099431f7_23_cout), .Aslc(Aslc), .Bslc(Bslc), .operation(opreation));
  ALU_1_bit_unit_099431f7 alu_1_bit_unit_099431f7_24 (
    .A(A[23]), .B(B[23]), .cin(alu_1_bit_unit_099431f7_23_cout), .reselt(R23),
    .cout(alu_1_bit_unit_099431f7_24_cout), .Aslc(Aslc), .Bslc(Bslc), .operation(opreation));
  ALU_1_bit_unit_099431f7 alu_1_bit_unit_099431f7_25 (
    .A(A[24]), .B(B[24]), .cin(alu_1_bit_unit_099431f7_24_cout), .reselt(R24),
    .cout(alu_1_bit_unit_099431f7_25_cout), .Aslc(Aslc), .Bslc(Bslc), .operation(opreation));
  ALU_1_bit_unit_099431f7 alu_1_bit_unit_099431f7_26 (
    .A(A[25]), .B(B[25]), .cin(alu_1_bit_unit_099431f7_25_cout), .reselt(R25),
    .cout(alu_1_bit_unit_099431f7_26_cout), .Aslc(Aslc), .Bslc(Bslc), .operation(opreation));
  ALU_1_bit_unit_099431f7 alu_1_bit_unit_099431f7_27 (
    .A(A[26]), .B(B[26]), .cin(alu_1_bit_unit_099431f7_26_cout), .reselt(R26),
    .cout(alu_1_bit_unit_099431f7_27_cout), .Aslc(Aslc), .Bslc(Bslc), .operation(opreation));
  ALU_1_bit_unit_099431f7 alu_1_bit_unit_099431f7_28 (
    .A(A[27]), .B(B[27]), .cin(alu_1_bit_unit_099431f7_27_cout), .reselt(R27),
    .cout(alu_1_bit_unit_099431f7_28_cout), .Aslc(Aslc), .Bslc(Bslc), .operation(opreation));
  ALU_1_bit_unit_099431f7 alu_1_bit_unit_099431f7_29 (
    .A(A[28]), .B(B[28]), .cin(alu_1_bit_unit_099431f7_28_cout), .reselt(R28),
    .cout(alu_1_bit_unit_099431f7_29_cout), .Aslc(Aslc), .Bslc(Bslc), .operation(opreation));
  ALU_1_bit_unit_099431f7 alu_1_bit_unit_099431f7_30 (
    .A(A[29]), .B(B[29]), .cin(alu_1_bit_unit_099431f7_29_cout), .reselt(R29),
    .cout(alu_1_bit_unit_099431f7_30_cout), .Aslc(Aslc), .Bslc(Bslc), .operation(opreation));
  ALU_1_bit_unit_099431f7 alu_1_bit_unit_099431f7_31 (
    .A(A[30]), .B(B[30]), .cin(alu_1_bit_unit_099431f7_30_cout), .reselt(R30),
    .cout(alu_1_bit_unit_099431f7_31_cout), .Aslc(Aslc), .Bslc(Bslc), .operation(opreation));
  ALU_1_bit_unit_099431f7 alu_1_bit_unit_099431f7_32 (
    .A(A[31]), .B(B[31]), .cin(alu_1_bit_unit_099431f7_31_cout), .reselt(R31), .cout(Cout), .Aslc(Aslc),
    .Bslc(Bslc), .operation(opreation));
  xor xor_1 (overflow, alu_1_bit_unit_099431f7_31_cout, Cout);
  Shifter #(.width(32)) shifter_1 (.in(A), .\dist (B[4:0]), .out(shifter_1_out));
  Shifter #(.width(32), .shift("lr")) shifter_2 (.in(A), .\dist (B[4:0]), .out(shifter_2_out));
  Shifter #(.width(32), .shift("ar")) shifter_3 (.in(A), .\dist (B[4:0]), .out(shifter_3_out));
  Shifter #(.width(32), .shift("rr")) shifter_4 (.in(A), .\dist (B[4:0]), .out(shifter_4_out));
  not not_1 (not_1_out, comparator_1_gt);
  Comparator #(.width(32)) comparator_1 (
    .a(A), .b(B), .gt(comparator_1_gt), .eq(comparator_1_eq), .lt(comparator_1_lt));
  not not_2 (not_2_out, comparator_1_eq);
  not not_3 (not_3_out, comparator_2_gt);
  Comparator #(.width(32), .mode("unsigned")) comparator_2 (
    .a(A), .b(B), .gt(comparator_2_gt), .eq(comparator_2_eq), .lt(comparator_2_lt));
  not not_4 (not_4_out, comparator_2_eq);
  assign bit_extender_1_out = {{31{1'b0}}, R31};  // Bit_Extender bit_extender_1
  and sign (sign_out, not_1_out, not_2_out, comparator_1_lt);
  and unsign (unsign_out, not_3_out, not_4_out, comparator_2_lt);
  assign bit_extender_2_out = {{31{1'b0}}, sign_out};  // Bit_Extender bit_extender_2
  assign bit_extender_3_out = {{31{1'b0}}, unsign_out};  // Bit_Extender bit_extender_3
  Multiplexer #(.select(3), .width(32), .enable("false")) multiplexer_1 (
    .in0({R31, R30, R29, R28, R27, R26, R25, R24, R23, R22, R21, R20, R19, R18, R17, R16, R15, R14, R13, R12, R11, R10, R9, R8, R7, R6, R5, R4, R3, R2, R1, R0}),
    .in1(shifter_1_out), .in2(shifter_2_out), .in3(shifter_3_out), .in4(shifter_4_out),
    .in5(bit_extender_2_out), .in6(bit_extender_3_out), .in7(bit_extender_1_out), .out(Aluout),
    .sel(Operation));
  not not_5 (Zeroflag, or_1_out);
  or or_1 (or_1_out, R0, R1, R2, R3, R4, R5, R6, R7, R8, R9, R10, R11, R12, R13, R14, R15, R16, R17, R18, R19, R20, R21, R22, R23, R24, R25, R26, R27, R28, R29, R30, R31);

  // Other names for the same wires on the sheet: b_t[4:0] = B[4:0]
endmodule

module Next_PC_2d420801 (
  input  [4:0] ImmL_5,
  input  [10:0] ImmU_11,
  input  [15:0] Imm_16,
  input  [1:0] PCsrc,
  input  [31:0] Rs1_Test_Input_554d0cdc
);

  wire clock_1_out;
  wire [19:0] adder_1_out, adder_2_out, bit_extender_1_out, multiplexer_1_out, PC_q;
  wire [31:0] adder_3_out, bit_extender_2_out, Rs1_q;

  Clock clock_1 (.out(clock_1_out));
  Register #(.width(20)) PC (.D(multiplexer_1_out), .Q(PC_q), .clk(clock_1_out));  // open: en, clr
  Adder #(.width(20)) adder_1 (.a(PC_q), .b(20'h1), .out(adder_1_out));  // open: cin, cout
  // Probe on adder_1_out
  assign bit_extender_1_out = {{4{ImmU_11[10]}}, {ImmU_11, ImmL_5}};  // Bit_Extender bit_extender_1
  assign bit_extender_2_out = {{16{Imm_16[15]}}, Imm_16};  // Bit_Extender bit_extender_2
  Register #(.width(32)) Rs1 (.D(Rs1_Test_Input_554d0cdc), .Q(Rs1_q), .clk(clock_1_out));  // open: en, clr
  Adder #(.width(20)) adder_2 (.a(adder_1_out), .b(bit_extender_1_out), .out(adder_2_out), .cin(1'b0));  // open: cout
  Adder #(.width(32)) adder_3 (.a(bit_extender_2_out), .b(Rs1_q), .out(adder_3_out), .cin(1'b0));  // open: cout
  // Probe on adder_2_out
  // Probe on adder_3_out[19:0]
  Multiplexer #(.select(2), .width(20), .enable("false")) multiplexer_1 (
    .in0(adder_1_out), .in1(adder_2_out), .in2(adder_3_out[19:0]), .out(multiplexer_1_out), .sel(PCsrc));  // open: in3

  // Notes on the sheet:
  //   PC + 1
  //   PC + 1
endmodule

module ALU_1_bit_unit_099431f7 (
  input  A,
  input  Aslc,
  input  B,
  input  Bslc,
  input  [1:0] operation,
  input  cin,
  output reselt,
  output cout
);

  wire adder_1_out, and_1_out, multiplexer_1_out, multiplexer_2_out, not_1_out, not_2_out, or_1_out;

  not not_1 (not_1_out, A);
  not not_2 (not_2_out, B);
  Multiplexer #(.enable("false")) multiplexer_1 (.in0(A), .in1(not_1_out), .out(multiplexer_1_out), .sel(Aslc));
  Multiplexer #(.enable("false")) multiplexer_2 (.in0(B), .in1(not_2_out), .out(multiplexer_2_out), .sel(Bslc));
  and and_1 (and_1_out, multiplexer_1_out, multiplexer_2_out);
  or or_1 (or_1_out, multiplexer_1_out, multiplexer_2_out);
  xor xor_1 (or_1_out, multiplexer_1_out, multiplexer_2_out);
  Adder #(.width(1)) adder_1 (.a(multiplexer_1_out), .b(multiplexer_2_out), .out(adder_1_out), .cin(cin), .cout(cout));
  Multiplexer #(.select(2), .enable("false")) multiplexer_3 (
    .in0(and_1_out), .in1(or_1_out), .in2(or_1_out), .in3(adder_1_out), .out(reselt), .sel(operation));
endmodule
